# Fritzing sketch rover_nano (saved by Fritzing 1.0.7)
breadboards: 1

parts:
  DHT1 = DHT22 Humidity and Temperature Sensor
  Part1 = Barometric Pressure Sensor - BMP180 Breakout (GY-68)
  M1 = RioRand LM2596
  Part3 = MQ-7 breakout
  BAT1 = BC9VPC [package=bc9vpc]
  Part2 = MQ-4
  R1 = Resistor [tolerance=±5% power=0.25W resistance=220 package=THT]
  Part4 = Arduino Nano (Rev3.0)

nets:
  VCC: DHT1.VDD, Part1.VCC, M1.Pin_3, Part3.VCC, Part2.VCC, R1.Pin_0, Part4.5V
  N1: DHT1.DATA, R1.Pin_1, Part4.D2
  GND: DHT1.GND, Part1.GND, M1.Pin_4, Part3.GND, Part2.GND, Part4.GND
  N2: Part1.SCL, Part4.A5
  N3: Part1.SDA, Part4.A4
  N4: M1.Pin_1, BAT1.V+
  N5: M1.Pin_2, BAT1.V-
  N6: Part3.AO, Part4.A1
  N7: Part2.AO, Part4.A0

custom parts:
  MQ-7 breakout: SKU: 101282
